# Fritzing sketch 02b_Touch_Sensor (saved by Fritzing 0.9.3b)
breadboards: 1

parts:
  LED1 = smd LED [color="Red (633nm)" package="0805 [SMD]"]
  M1 = DOIT Esp32 DevKit v1 (30 pins long, 11 pins width) [part_number=ESP32S-PIN30]

nets:
  N1: LED1.cathode, M1.GND
  N2: LED1.anode, M1.D32

notes:
  Touch Wire

custom parts:
  DOIT Esp32 DevKit v1 (30 pins long, 11 pins width): The DOIT Esp32 DevKit v1 is one of the development board created by DOIT to evaluate the ESP-WROOM-32 module. It is based on the ESP32 microcontroller that boasts Wifi, Bluetooth, Ethernet and Low Power support all in a single chip. (vanepp) made breadboard work, adjusted pin numbering and labels and reduced size of schematic and cleaned up pcb. This chip is 30pins long (2 x15) and 11 pins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
